// Logisim project tp4.circ as structural Verilog
module main (
);

  wire button_1_out, clock_1_out, convertisseur_1_bot, convertisseur_1_center, convertisseur_1_l_h,
       convertisseur_1_l_l, convertisseur_1_r_h, convertisseur_1_r_l, convertisseur_1_top,
       convertisseur_2_bot, convertisseur_2_center, convertisseur_2_l_h, convertisseur_2_l_l,
       convertisseur_2_r_h, convertisseur_2_r_l, convertisseur_2_top, convertisseur_3_bot,
       convertisseur_3_center, convertisseur_3_l_h, convertisseur_3_l_l, convertisseur_3_r_h,
       convertisseur_3_r_l, convertisseur_3_top, lcs_1_c_out, lcs_1_high, lcs_1_low, lcs_2_c_out, lcs_2_high,
       lcs_2_low, lcs_3_high, lcs_3_low, undriven;

  Clock clock_1 (.out(clock_1_out));
  Button button_1 (.out(button_1_out));
  LCS lcs_1 (
    .Clock(clock_1_out), .C_IN(1'b1), .Reset(button_1_out), .C_OUT(lcs_1_c_out), .Low(lcs_1_low),
    .High(lcs_1_high));
  LCS lcs_2 (
    .Clock(clock_1_out), .C_IN(lcs_1_c_out), .Reset(button_1_out), .C_OUT(lcs_2_c_out), .Low(lcs_2_low),
    .High(lcs_2_high));
  LCS lcs_3 (
    .Clock(clock_1_out), .C_IN(lcs_2_c_out), .Reset(button_1_out), .Low(lcs_3_low), .High(lcs_3_high));  // open: C_OUT
  Convertisseur convertisseur_1 (
    .a(undriven), .b(lcs_1_low), .c(lcs_1_high), .center(convertisseur_1_center), .L_H(convertisseur_1_l_h),
    .top(convertisseur_1_top), .R_H(convertisseur_1_r_h), .R_L(convertisseur_1_r_l),
    .BOT(convertisseur_1_bot), .L_L(convertisseur_1_l_l));
  Convertisseur convertisseur_2 (
    .b(lcs_2_low), .c(lcs_2_high), .center(convertisseur_2_center), .L_H(convertisseur_2_l_h),
    .top(convertisseur_2_top), .R_H(convertisseur_2_r_h), .R_L(convertisseur_2_r_l),
    .BOT(convertisseur_2_bot), .L_L(convertisseur_2_l_l));  // open: a
  Convertisseur convertisseur_3 (
    .b(lcs_3_low), .c(lcs_3_high), .center(convertisseur_3_center), .L_H(convertisseur_3_l_h),
    .top(convertisseur_3_top), .R_H(convertisseur_3_r_h), .R_L(convertisseur_3_r_l),
    .BOT(convertisseur_3_bot), .L_L(convertisseur_3_l_l));  // open: a
  _7_Segment_Display u_7_segment_display_1 (
    .g(convertisseur_1_center), .f(convertisseur_1_l_h), .a(convertisseur_1_top), .b(convertisseur_1_r_h),
    .e(convertisseur_1_l_l), .d(convertisseur_1_bot), .c(convertisseur_1_r_l), .dp(1'b0));
  _7_Segment_Display u_7_segment_display_2 (
    .g(convertisseur_2_center), .f(convertisseur_2_l_h), .a(convertisseur_2_top), .b(convertisseur_2_r_h),
    .e(convertisseur_2_l_l), .d(convertisseur_2_bot), .c(convertisseur_2_r_l), .dp(1'b0));
  _7_Segment_Display u_7_segment_display_3 (
    .g(convertisseur_3_center), .f(convertisseur_3_l_h), .a(convertisseur_3_top), .b(convertisseur_3_r_h),
    .e(convertisseur_3_l_l), .d(convertisseur_3_bot), .c(convertisseur_3_r_l), .dp(1'b0));
endmodule

module LBS (
  input  Clock,
  input  C_in,
  input  Reset,
  output C_out,
  output one,
  output two,
  output three
);

  wire and_1_out, nand_1_out, or_1_out;

  and and_1 (and_1_out, Clock, C_in);
  nand nand_1 (nand_1_out, or_1_out, Clock);
  or or_1 (or_1_out, three, two, one);
  D_Flip_Flop d_ff_1 (.D(nand_1_out), .clk(and_1_out), .Q(one), .reset(Reset));  // open: Qn, preset
  D_Flip_Flop d_ff_2 (.D(one), .clk(and_1_out), .Q(two), .reset(Reset));  // open: Qn, preset
  D_Flip_Flop d_ff_3 (.D(two), .clk(and_1_out), .Q(three), .reset(Reset));  // open: Qn, preset
  and and_2 (C_out, C_in, three);
endmodule

module LCS (
  input  Clock,
  input  C_IN,
  input  Reset,
  output C_OUT,
  output Low,
  output High
);

  wire and_1_out, and_2_out, d_ff_3_q, nand_1_out, nand_2_out, or_1_out;

  and and_1 (and_1_out, Clock, C_IN);
  nand nand_1 (nand_1_out, or_1_out, Clock);
  or or_1 (or_1_out, High, Low);
  D_Flip_Flop d_ff_1 (.D(nand_1_out), .clk(and_1_out), .Q(Low), .reset(Reset));  // open: Qn, preset
  D_Flip_Flop d_ff_2 (.D(Low), .clk(and_1_out), .Q(High), .reset(Reset));  // open: Qn, preset
  nand nand_2 (nand_2_out, d_ff_3_q, Clock);
  and and_2 (and_2_out, High, Clock);
  D_Flip_Flop #(.trigger("falling")) d_ff_3 (
    .D(nand_2_out), .clk(and_2_out), .Q(d_ff_3_q), .reset(Reset));  // open: Qn, preset
  and and_3 (C_OUT, C_IN, d_ff_3_q);
endmodule

module Convertisseur (
  input  a,
  input  b,
  input  c,
  output center,
  output L_H,
  output top,
  output R_H,
  output R_L,
  output BOT,
  output L_L
);

  wire not_1_out, not_2_out;

  not not_1 (not_1_out, b);
  not not_2 (not_2_out, c);
  not not_3 (top, b);
  not not_4 (R_L, c);
  not not_5 (BOT, b);
  not not_6 (L_L, b);
  and and_1 (L_H, not_1_out, not_2_out);

  assign center = c;
  assign R_H = 1'b1;
endmodule
